# Fritzing sketch boriattino_esp32 (saved by Fritzing 1.0.2b)
circuit board: 8.46667cm x 5.64444cm
breadboards: 1

parts:
  sdCard1 = my_sdCard
  Componente1 = InvenSense MPU6050
  M2 = v.Kel GPS module
  HC-1 = HC-12 Module
  M1 = DOIT Esp32 DevKit v1 (30 pins long, 11 pins width) [part_number=ESP32S-PIN30]
  LED1 = smd LED [color="Red (633nm)" package="0603 [SMD]"]
  LED2 = smd LED [color="Green (570nm)" package="0603 [SMD]"]
  R1 = Resistor [tolerance=±5% power=0.25W resistance=220 package=THT]
  R2 = Resistor [tolerance=±5% power=0.25W resistance=220 package=THT]
  Bat1 = battery_holder_single_18650
  TP1 = TP4056 [chip_label=TP4056 package="DIP (Dual Inline) [THT]"]
  MOD1 = MT3608 Boost No usb
  SW1 = Slide_Switch_new
  J1 = USB type C-05-power-only

nets:
  GND: sdCard1.GND, Componente1.GND, M2.Pin_2, HC-1.GND, M1.GND, LED1.anode, LED2.anode, TP1.pin6, MOD1.IN_(-), MOD1.OUT_(-)
  VCC: sdCard1.VCC, Componente1.VCC, M2.Pin_5, HC-1.VCC, M1.3V3
  N1: sdCard1.MISO, M1.D19
  N2: sdCard1.MOSI, M1.D23
  N3: sdCard1.SCK, M1.D18
  N4: sdCard1.CS, M1.D5
  N5: Componente1.SCL, M1.D22
  N6: Componente1.SDA, M1.D21
  N7: M2.Pin_3, M1.TX2
  N8: M2.Pin_4, M1.RX2
  N9: HC-1.TXD, M1.D4, M1.D35
  N10: HC-1.RXD, M1.D2, M1.D32
  N11: M1.D33, R1.Pin_0
  N12: M1.D27, R2.Pin_0
  N13: M1.VIN, SW1.pin_1
  N14: LED1.cathode, R2.Pin_1
  N15: LED2.cathode, R1.Pin_1
  N16: Bat1.+#0, TP1.pin5
  N17: Bat1.+#1, TP1.pin4
  N18: TP1.pin1, J1.Pin_3
  N19: TP1.pin2, J1.Pin_1, J1.Pin_4
  N20: TP1.pin3, MOD1.IN_(+)
  N21: MOD1.OUT_(+), SW1.pin_2

custom parts:
  my_sdCard: micro sdCard Adapter with 90º pin header. Use a filtering Capacitor between CS and GND if needed. PCB View Pinouts are Reversed for laying parallel on PCB using a 90º pin header.
  v.Kel GPS module: Generic v.Kel GPS module
  HC-12 Module: HC-12 433Mhz Module
  DOIT Esp32 DevKit v1 (30 pins long, 11 pins width): The DOIT Esp32 DevKit v1 is one of the development board created by DOIT to evaluate the ESP-WROOM-32 module. It is based on the ESP32 microcontroller that boasts Wifi, Bluetooth, Ethernet and Low Power support all in a single chip. (vanepp) made breadboard work, adjusted pin numbering and labels and reduced size of schematic and cleaned up pcb. This chip is 30pins long (2 x15) and 11 pins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
  battery_holder_single_18650: single 18650 battery holder
  TP4056: A DIP stand-in part for whatever IC you want. With 6 pins on a 300mil dual inline package (DIP) footprint.
  MT3608 Boost No usb: Chip- MT3608 / B6289 DC to DC step up, power booster module. With adjustable output voltage. Current- 2A . || Input voltage- 2V-24V || Output voltage- 5V-28V Input interface- Inversed polarity- NO. || Led indicator- No.
  Slide_Switch_new: the New two pin slide switch
